# Fritzing sketch Arbetskrav2-Alarm.v2 (saved by Fritzing 0.9.10b)
breadboards: 2

parts:
  Part2 = Arduino Uno (Rev3)
  Keypad4x1 = Keypad Membran 4x4
  J1 = Piezo Speaker
  R1 = Resistor [tolerance=±5% resistance=330 package="1206 [SMD]"]
  ZS-042_RTC1 = ZS-042 RTC Module
  HC-SR04_Sensor_1 = HC-SR04 Ultrasonic Distance Sensor
  Part3 = Adafruit 1.3in 240x240 IPS TFT [part_number="Adafruit #4313"]
  R2 = Resistor [tolerance=±5% resistance=1k package="1206 [SMD]"]
  R3 = Resistor [tolerance=±5% resistance=1k package="1206 [SMD]"]
  R4 = Resistor [tolerance=±5% resistance=1k package="1206 [SMD]"]
  R5 = Resistor [tolerance=±5% resistance=1k package="1206 [SMD]"]
  R6 = Resistor [tolerance=±5% resistance=220 package="1206 [SMD]"]
  R7 = Resistor [tolerance=±5% resistance=220 package="1206 [SMD]"]
  R8 = Resistor [tolerance=±5% resistance=220 package="1206 [SMD]"]
  R10 = Resistor [tolerance=±5% resistance=10k package="1206 [SMD]"]

nets:
  N1: Part2.A0, HC-SR04_Sensor_1.TRIG
  N2: Part2.A1, HC-SR04_Sensor_1.ECHO
  N3: Part2.A2, J1.pin2
  N4: Part2.A3, Keypad4x1.Pin5, R6.Pin_0, R10.Pin_1
  N5: Part2.D8, Part3.TFTDC
  N6: Part2.D10_PWM/SS, Part3.TFTCS
  N7: Part2.D11_PWM/MOSI, Part3.MOSI
  N8: Part2.D12/MISO, Part3.MISO
  N9: Part2.D13/SCK, Part3.SCK
  N10: Part2.A4/SDA, ZS-042_RTC1.SDA
  N11: Part2.A5/SCL, ZS-042_RTC1.SCL
  N12: Part2.D4, Part3.CARDCS
  VCC: Part2.5V, ZS-042_RTC1.VCC, HC-SR04_Sensor_1.VCC, Part3.VIN, R3.Pin_1
  GND: Part2.GND, R1.Pin_0, ZS-042_RTC1.GND, HC-SR04_Sensor_1.GND, Part3.GND, R10.Pin_0
  N13: Keypad4x1.Pin1, R3.Pin_0, R5.Pin_0
  N14: Keypad4x1.Pin2, R4.Pin_0, R5.Pin_1
  N15: Keypad4x1.Pin3, R2.Pin_0, R4.Pin_1
  N16: Keypad4x1.Pin4, R2.Pin_1
  N17: Keypad4x1.Pin6, R6.Pin_1, R7.Pin_0
  N18: Keypad4x1.Pin7, R7.Pin_1, R8.Pin_0
  N19: Keypad4x1.Pin8, R8.Pin_1
  N20: J1.pin1, R1.Pin_1

custom parts:
  Keypad Membran 4x4: Membrane Keypad 4x4 Matrix
  Adafruit 1.3in 240x240 IPS TFT: We've been looking for a display like this for a long time - it's so small only 1.3" diagonal but has a high density 260 ppi, 240x240 pixel display with full-angle viewing. It looks a lot like our 1.44" 128x128 display, but has 4x as many pixels and looks great at any angle. We've seen displays of this caliber used in smartwatches and small electronic devices but they've always been MIPI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
